# Fritzing sketch coin_led (saved by Fritzing 0.9.3b)
breadboards: 1

parts:
  R1 = Resistor [tolerance=±5% resistance=220 package=THT]
  Part1 = Arduino Uno (Rev3)
  S1 = Pushbutton [package="[THT]"]

nets:
  N1: R1.Pin_0, Part1.D13/SCK, S1.Pin_3, S1.Pin_4
  N2: R1.Pin_1, Part1.5V
  N3: Part1.GND, S1.Pin_1, S1.Pin_2
