# Fritzing sketch ds1302 (saved by Fritzing 0.8.7b)
breadboards: 1

parts:
  module2 = I2C LCD1602
  元件1 = Arduino Uno (Rev3) - ICSP
  module3 = DS1302-v1.0

nets:
  N1: module2.SCL, 元件1.A5/SCL
  N2: module2.SDA, 元件1.A4/SDA
  VCC: module2.VCC, 元件1.5V, module3.VCC
  GND: module2.GND, 元件1.GND, module3.GND
  N3: 元件1.D5_PWM, module3.RST
  N4: 元件1.D6_PWM, module3.DAT
  N5: 元件1.D7, module3.CLK

notes:
  DS1302 Module

custom parts:
  I2C LCD1602: I2C LCD1602 module of SunFounder Sensor Kit
  DS1302-v1.0: DS1302 module of SunFounder Sensor Kit
